// Logisim project alu.circ as structural Verilog: 1 circuit, main circuit alu
module alu (
  input  [31:0] A,
  input  [31:0] B,
  input  [3:0] ALUSel,
  output [31:0] Result
);

  wire comparator_1_lt, xor_1_out;
  wire [31:0] add0, and0, divu0, mul0, mulh0, mulhu0, multiplexer_1_out, multiplexer_2_out,
       multiplier_1_cout, negator_1_out, negator_2_out, negator_3_out, or0, remu0, sll0, slt0, sra0, srl0,
       sub0, subtractor_1_out, xor0;

  Negator #(.width(32)) negator_1 (.in(A), .out(negator_1_out));
  Negator #(.width(32)) negator_2 (.in(B), .out(negator_2_out));
  Multiplexer #(.width(32), .enable("false")) multiplexer_1 (
    .in0(A), .in1(negator_1_out), .out(multiplexer_1_out), .sel(A[31]));
  Multiplexer #(.width(32), .enable("false")) multiplexer_2 (
    .in0(B), .in1(negator_2_out), .out(multiplexer_2_out), .sel(B[31]));
  Multiplier #(.width(32)) multiplier_1 (
    .a(multiplexer_1_out), .b(multiplexer_2_out), .cout(multiplier_1_cout));  // open: out, cin
  xor xor_1 (xor_1_out, A[31], B[31]);
  Negator #(.width(32)) negator_3 (.in(multiplier_1_cout), .out(negator_3_out));
  Subtractor #(.width(32)) subtractor_1 (.a(negator_3_out), .b(32'h1), .out(subtractor_1_out));  // open: bin, bout
  Adder #(.width(32)) adder_1 (.a(A), .b(B), .out(add0));  // open: cin, cout
  assign and0 = A & B;  // AND_Gate and_1, 32 bits wide
  assign or0 = A | B;  // OR_Gate or_1, 32 bits wide
  assign xor0 = A ^ B;  // XOR_Gate xor_2, 32 bits wide
  Shifter #(.width(32), .shift("lr")) shifter_1 (.in(A), .\dist (B[4:0]), .out(srl0));
  Shifter #(.width(32), .shift("ar")) shifter_2 (.in(A), .\dist (B[4:0]), .out(sra0));
  Shifter #(.width(32)) shifter_3 (.in(A), .\dist (B[4:0]), .out(sll0));
  Comparator #(.width(32)) comparator_1 (.a(A), .b(B), .lt(comparator_1_lt));  // open: gt, eq
  Multiplexer #(.width(32), .enable("false")) multiplexer_3 (
    .in0(multiplier_1_cout), .in1(subtractor_1_out), .out(mulh0), .sel(xor_1_out));
  assign slt0 = {{31{1'b0}}, comparator_1_lt};  // Bit_Extender bit_extender_1
  Divider #(.width(32)) divider_1 (.a(A), .b(B), .out(divu0), .rem(remu0));  // open: upper
  Multiplier #(.width(32)) multiplier_2 (.a(A), .b(B), .out(mul0), .cout(mulhu0));  // open: cin
  Subtractor #(.width(32)) subtractor_2 (.a(A), .b(B), .out(sub0));  // open: bin, bout
  Multiplexer #(.select(4), .width(32), .enable("false")) multiplexer_4 (
    .in0(add0), .in1(and0), .in2(or0), .in3(xor0), .in4(srl0), .in5(sra0), .in6(sll0), .in7(slt0),
    .in8(divu0), .in9(remu0), .in10(mul0), .in11(mulhu0), .in12(sub0), .in13(B), .in14(mulh0), .out(Result),
    .sel(ALUSel));  // open: in15

  // Other names for the same wires on the sheet: ASign = A[31]; bsel0[31:0] = B; BSign = B[31]

  // Notes on the sheet:
  //   INPUTS to your circuit
  //   DON'T CHANGE THE LOCATIONS OF THE INPUTS AND OUTPUTS!
  //   OUTPUT from your circuit
endmodule
